# Fritzing sketch DriveSystem (saved by Fritzing 0.9.3b)

parts:
  U4 = MCP41xxx [package=so08]  # not connected
  RE1 = Rotary Encoder [package=THT]
  RE2 = Rotary Encoder [package=THT]
  Part1 = Arduino Mega 2560 (Rev3)
  U6 = 941H-2C-5D [package=relay-5v]
  U7 = 941H-2C-5D [package=relay-5v]
  U8 = RELAY [package=OJ]

nets:
  N1: RE1.EncoderPinA, Part1.D18/TX1
  N2: RE1.EncoderPinC, RE2.EncoderPinC, Part1.5V
  N3: RE1.EncoderPinB, Part1.D19/RX1
  N4: RE2.EncoderPinA, Part1.D20/SDA
  N5: RE2.EncoderPinB, Part1.D21/SCL
  N6: Part1.GND, U6.16, U7.16
  N7: Part1.D4_PWM, U7.1
  N8: Part1.D5_PWM, U8.NO
  N9: U6.1, U8.MAIN
  N10: U6.8, U7.13
  N11: U6.9, U7.4

notes:
  Direction Control
  Input Select
  E-Stop switch to manual
  Left Wheel Encoder
  Right Wheel Encoder

custom parts:
  941H-2C-5D: DPDT Relay - 2 Form C
